# Fritzing sketch sirene (saved by Fritzing 0.9.3b)
breadboards: 1

parts:
  Bauteil1 = Arduino Uno (Rev3)
  Q1 = Basic FET N-Channel [package="D2Pak [SMD]"]
  SP1 = SPEAKER [package=pcb_mount_speaker]
  U1 = LIPO-2000mAh [package=lipo-2000]
  U2 = LIPO-2000mAh [package=lipo-2000]
  U3 = LIPO-2000mAh [package=lipo-2000]
  U4 = LIPO-2000mAh [package=lipo-2000]

nets:
  N1: Bauteil1.D9_PWM, Q1.Gate
  N2: Bauteil1.GND, Q1.drain, U1.-
  N3: Bauteil1.VIN, SP1.-, U3.+
  N4: Q1.source, SP1.+
  N5: U1.+, U4.-
  N6: U2.+, U3.-
  N7: U2.-, U4.+
